# Fritzing sketch sls (saved by Fritzing 0.9.3b)
breadboards: 1

parts:
  U1 = NodeMCU V1.0
  R1 = Resistor [tolerance=±5% resistance=10k package="0402 [SMD]"]
  R2 = PHOTOCELL [package=photocell-kit]

nets:
  N1: U1.3V3, R1.Pin_0
  N2: U1.GND, R2.P$2
  N3: U1.A0, R1.Pin_1, R2.P$1

custom parts:
  NodeMCU V1.0: ESP8266 based NodeMCU
